# Fritzing sketch Circuito (saved by Fritzing 0.9.5d)

parts:
  Part1 = Arduino Nano (Rev3.0)
  U1 = LIPO-1000mAh [package=lipo-1000]
  TP1 = TP4056 [chip_label=TP4056 package="DIP (Dual Inline) [THT]"]
  S1 = Pushbutton [package="[THT]"]
  S2 = Pushbutton [package="[THT]"]
  R2 = Resistor [tolerance=±5% resistance=1000 package="0402 [SMD]"]
  Part2 = Bluetooth HC-05 Macho
  R3 = Resistor [tolerance=±5% resistance=1000 package="0402 [SMD]"]  # not connected
  R4 = Resistor [tolerance=±5% resistance=1000 package="0402 [SMD]"]  # not connected
  R5 = Resistor [tolerance=±5% resistance=220 package="1206 [SMD]"]  # not connected
  R5_2 = Resistor [tolerance=±5% resistance=1000 package="2010 [SMD]"]
  S3 = Toggle Switch [package=THT]

nets:
  GND: Part1.GND, TP1.pin6, S1.Pin_3, S1.Pin_4, S2.Pin_3, S2.Pin_4, Part2.GND
  N1: Part1.D3, S2.Pin_2, R2.Pin_1
  N2: Part1.D4, S1.Pin_1, S1.Pin_2, R5_2.Pin_1
  N3: Part1.D10, Part2.TXD
  N4: Part1.D11/MOSI, Part2.RXD
  3V3: Part1.3V3, TP1.pin3, R2.Pin_0, Part2.VCC, R5_2.Pin_0
  N5: U1.+, TP1.pin4
  N6: U1.-, S3.L1
  N7: TP1.pin5, S3.COM

custom parts:
  TP4056: A DIP stand-in part for whatever IC you want. With 6 pins on a 300mil dual inline package (DIP) footprint.
